# Fritzing sketch Schematic (saved by Fritzing 1.0.4)

parts:
  A1 = ESP32-S3 zero
  RGB_SMD_LED1 = SMD RGB LED (WS2812) [package=5050]
  A2 = Esp32-c3 super mini
  RGB_SMD_LED2 = SMD RGB LED (WS2812) [package=5050]
  S1 = Cherry MX Blue [mn=Cherry mpn=MX1A-E1NW]
  S2 = Cherry MX Blue [mn=Cherry mpn=MX1A-E1NW]

nets:
  N1: A1.Pin_1, RGB_SMD_LED1.VCC
  N2: A1.Pin_2, RGB_SMD_LED1.VSS
  N3: A1.Pin_3, S1.pin_2
  N4: A1.Pin_4, S1.pin_1
  N5: A1.Pin_5, RGB_SMD_LED1.DIn
  N6: A2.Pin_12, RGB_SMD_LED2.DIn
  N7: A2.Pin_13, S2.pin_1
  N8: A2.Pin_14, S2.pin_2
  N9: A2.Pin_15, RGB_SMD_LED2.VSS
  N10: A2.Pin_16, RGB_SMD_LED2.VCC

notes:
  - S3 Zero -
  Button = GPIO 1
  LED = GPIO 2
  - C3 Zero -
  Button = GPIO 0
  LED = GPIO 1
  - S3 SuperMini -
  Button = GPIO 13
  LED = GPIO 12
  - C3 SuperMini -
  Button = GPIO 4
  LED = GPIO 3

custom parts:
  ESP32-S3 zero: ESP32-S3 Mini Development Board, Based on ESP32-S3FH4R2 Dual-Core Processor, 240MHz Running Frequency, 2.4GHz Wi-Fi & Bluetooth 5.
  Esp32-c3 super mini: ESP32-C3 Development Board ESP32 SuperMini Development Board ESP32 Development Board WiFi Bluetooth.
  Cherry MX Blue: Cherry MX Blue Keyswitch button for keyboards
